// Logisim project COUNTER_var16.circ as structural Verilog: 1 circuit, main circuit main
module main (
  input  A,
  input  B
);

  wire clock_1_out, newQ0, newQ1, newQ2, newQ3, not_1_out, not_2_out, R1, R2, R3, R4, R5, R6, st0, st1, st2,
       st3, st4, st5, st6, st7, st8, st9, st10, st11, st12, st13, st14, st15;
  wire [3:0] nQ, Q;

  not not_1 (not_1_out, A);
  not not_2 (not_2_out, B);
  and and_1 (R1, A, st11);
  and and_2 (R2, not_1_out, st11);
  and and_3 (R3, B, st4);
  and and_4 (R4, not_2_out, st4);
  and and_5 (R5, B, st1);
  and and_6 (R6, not_2_out, st1);
  Clock clock_1 (.out(clock_1_out));
  and _0 (st0, nQ[0], nQ[1], nQ[2], nQ[3]);
  and _1 (st1, Q[0], nQ[1], nQ[2], nQ[3]);
  and _2 (st2, nQ[0], Q[1], nQ[2], nQ[3]);
  and _3 (st3, Q[0], Q[1], nQ[2], nQ[3]);
  and _4 (st4, nQ[0], nQ[1], Q[2], nQ[3]);
  and _5 (st5, Q[0], nQ[1], Q[2], nQ[3]);
  and _6 (st6, nQ[0], Q[1], Q[2], nQ[3]);
  and _7 (st7, Q[0], Q[1], Q[2], nQ[3]);
  D_Flip_Flop d_ff_1 (.clk(clock_1_out), .D(newQ3), .Q(Q[3]), .Qn(nQ[3]));  // open: preset, en, reset
  D_Flip_Flop d_ff_2 (.clk(clock_1_out), .D(newQ2), .Q(Q[2]), .Qn(nQ[2]));  // open: preset, en, reset
  and _8 (st8, nQ[0], nQ[1], nQ[2], Q[3]);
  and _9 (st9, Q[0], nQ[1], nQ[2], Q[3]);
  and _10 (st10, nQ[0], Q[1], nQ[2], Q[3]);
  and _11 (st11, Q[0], Q[1], nQ[2], Q[3]);
  and _12 (st12, nQ[0], nQ[1], Q[2], Q[3]);
  and _13 (st13, Q[0], nQ[1], Q[2], Q[3]);
  and _14 (st14, nQ[0], Q[1], Q[2], Q[3]);
  and _15 (st15, Q[0], Q[1], Q[2], Q[3]);
  D_Flip_Flop d_ff_3 (.clk(clock_1_out), .D(newQ1), .Q(Q[1]), .Qn(nQ[1]));  // open: preset, en, reset
  D_Flip_Flop d_ff_4 (.clk(clock_1_out), .D(newQ0), .Q(Q[0]), .Qn(nQ[0]));  // open: preset, en, reset
  or u_newQ1 (newQ1, st3, st0, R4, st7, st8, st2, st9, R5, R2, st3);
  or u_newQ2 (newQ2, R1, st15, R3, st6, st7, st8, st2, st9, R2, R1);
  Hex_Digit_Display hex_digit_display_1 (.value(Q));  // open: dp
  or u_newQ3 (newQ3, st10, st13, R4, R3, st8, st14, st2, st9, R6, R1, st3);
  or u_newQ0 (newQ0, st0, st15, R3, st8, R6, st12, R2, st3);
  Bit_Extender bit_extender_1 ();  // open: in, out

  // Notes on the sheet:
  //   Шина для прямых выходов
  //   Шина для инверсных выходов
endmodule
